# Fritzing sketch CBA_2020_09_24 (saved by Fritzing 0.9.4)
circuit board: 10cm x 10cm
breadboards: 1

parts:
  J1 = STM32F103C8T6 blue mini board
  LEDbar = LED_BARGRAPH_10 [package=led_bargaph_10]
  J3 = female pin header, 2 pins [form="♀ (female)"]
  R12 = Resistor [tolerance=±5% resistance=220 package="0603 [SMD]"]
  R13 = Resistor [tolerance=±5% resistance=220 package="0603 [SMD]"]
  R14 = Resistor [tolerance=±5% resistance=220 package="0603 [SMD]"]
  R15 = Resistor [tolerance=±5% resistance=220 package="0603 [SMD]"]
  R16 = Resistor [tolerance=±5% resistance=220 package="0603 [SMD]"]
  R17 = Resistor [tolerance=±5% resistance=220 package="0603 [SMD]"]
  R18 = Resistor [tolerance=±5% resistance=220 package="0603 [SMD]"]
  R19 = Resistor [tolerance=±5% resistance=220 package="0603 [SMD]"]
  R20 = Resistor [tolerance=±5% resistance=220 package="0603 [SMD]"]
  R21 = Resistor [tolerance=±5% resistance=220 package="0603 [SMD]"]
  S1 = JOYSTICK_MINI [package=joystick_mini]
  B5 = male pin header, 3 pins [form="♂ (male)"]
  B6 = male pin header, 2 pins [form="♂ (male)"]
  B7 = male pin header, 2 pins [form="♂ (male)"]
  B4 = male pin header, 2 pins [form="♂ (male)"]
  B2 = male pin header, 6 pins [form="♂ (male)"]
  BME280 = BME280r2 [package=lga8]  # not connected
  PCF8574 = PCF8574 [package="DIP16 [THT]"]  # not connected
  Joystick = Thumb Joystick [package=joystick]  # not connected
  U5 = MCP73831 [package=sot23-5]
  JP1 = Header 2 [package=jst-2-pth-kit]
  R22 = Resistor [tolerance=±5% resistance=10k package="0603 [SMD]"]
  PC13 = smd LED [color="Green (560nm)" package="0603 [SMD]"]  # not connected
  PWR1 = smd LED [color="Red (633nm)" package="0603 [SMD]"]  # not connected
  D2 = DIODE-SCHOTTKY [package=sma-diode]
  74VHC125MTC = TSSOP14 [chip_label=IC package=TSSOP]  # not connected
  OLED = 27 pin OLED  # not connected
  LM75 = MSOP8 [chip_label=IC package=MSOP8]  # not connected
  Buzzer = Buzzer 12mm [package=buzzer-cmt1102]  # not connected
  Flash = SPI_FLASH-X25XX [package=so08]  # not connected
  7_SegmentG1 = 7 Segment DisplayG

nets (from the pcb view):
  N1: J1.A8, B5.pin1
  N2: J1.A9, B2.pin2
  N3: J1.A10, B2.pin3
  N4: J1.B5, S1.CENT
  N5: J1.B6, S1.UP
  N6: J1.B7, S1.DOWN
  5V: J1.5V, B5.pin2, U5.VIN, D2.C
  GND: J1.G, J1.GND, S1.GND, B5.pin3, B2.pin6, U5.VSS, JP1.1, R22.Pin_0
  N7: J1.3.3V, B4.pin1
  N8: J1.A0, LEDbar.A_C
  N9: J1.A1, LEDbar.B_C
  N10: J1.A2, LEDbar.C_C
  N11: J1.A3, LEDbar.D_C
  N12: J1.A4, LEDbar.E_C
  N13: J1.A5, LEDbar.F_C
  N14: J1.A6, LEDbar.G_C
  N15: J1.A7, LEDbar.H_C
  N16: J1.B0, B7.pin1
  N17: J1.B1, B6.pin1
  N18: LEDbar.I_A, R20.Pin_0
  N19: LEDbar.J_A, R21.Pin_0
  N20: LEDbar.J_C, J3.pin1
  N21: LEDbar.I_C, J3.pin2
  N22: R12.Pin_0, 7_SegmentG1.Segment_A
  N23: R13.Pin_0, 7_SegmentG1.Segment_B
  N24: R14.Pin_0, 7_SegmentG1.Segment_C
  N25: R15.Pin_1, 7_SegmentG1.Segment_D
  N26: R16.Pin_1, 7_SegmentG1.Segment_E
  N27: R17.Pin_1, 7_SegmentG1.Segment_F
  N28: R18.Pin_1, 7_SegmentG1.Segment_G
  N29: R19.Pin_0, 7_SegmentG1.Segment_DP
  N30: R20.Pin_1, R21.Pin_1, B4.pin2
  N31: S1.RIGHT, B7.pin2
  N32: S1.LEFT, B6.pin2
  N33: U5.VBAT, JP1.2, D2.A
  N34: U5.PROG, R22.Pin_1

notes:
  PA0
  G
  G G3.3
  VBAT
  3.3
  RX
  TX
  5V G
  CBA_2020_09_24

custom parts:
  7 Segment DisplayG: 7 Segment Display with common cathode.(fixed G)
